# Fritzing sketch ultrasonic_rangefinder (saved by Fritzing 0.9.2b)
breadboards: 1

parts:
  Part1 = SRF05 Ultrasonic Rangefinder
  R1 = Resistor [tolerance=±5% resistance=100 package="0603 [SMD]"]
  R2 = Resistor [tolerance=±5% resistance=220 package="0603 [SMD]"]
  Raspberry_Pi1 = Raspberry Pi 2
  R3 = Resistor [tolerance=±5% resistance=470 package="0603 [SMD]"]

nets:
  VCC: Part1.VCC, Raspberry_Pi1.5V
  N1: Part1.Trig, Raspberry_Pi1.GPIO4
  N2: Part1.Echo, R1.Pin_1
  GND: Part1.GND, Raspberry_Pi1.GND, R3.Pin_1
  N3: R1.Pin_0, R2.Pin_0
  N4: R2.Pin_1, Raspberry_Pi1.GPIO17, R3.Pin_0
